# Fritzing sketch RPi_LCD_Java (saved by Fritzing 0.8.7b)
circuit board: 8.46667cm x 5.64444cm
breadboards: 1

parts:
  R1 = Trimmer Potentiometer [maximum_resistance=10kΩ package=THT]
  LCD1 = LCD screen
  Raspberry_Pi_B_rev1 = Raspberry Pi B rev2

nets:
  VDD: R1.leg1, LCD1.VDD, LCD1.LED+, Raspberry_Pi_B_rev1.5V
  N1: R1.wiper, LCD1.V0
  VSS: R1.leg2, LCD1.VSS, LCD1.R/W, LCD1.DB7, LCD1.LED-, Raspberry_Pi_B_rev1.GND
  N2: LCD1.RS, Raspberry_Pi_B_rev1.GPIO_7
  N3: LCD1.E, Raspberry_Pi_B_rev1.GPIO_8
  N4: LCD1.DB4, Raspberry_Pi_B_rev1.GPIO_17
  N5: LCD1.DB5, Raspberry_Pi_B_rev1.GPIO_18
